# Fritzing sketch lm35 (saved by Fritzing 0.9.4)
breadboards: 1

parts:
  Part1 = Arduino Uno (Rev3)
  LED1 = LED - 5mm [color="Red (633nm)" package="5 mm [THT]"]
  T1 = LM35 Temperature Sensor [package="TO92 [THT]"]
  R1 = Resistor [tolerance=±5% resistance=220 package=THT]

nets:
  N1: Part1.A0, T1.Vout
  GND: Part1.GND, T1.GND, R1.Pin_0
  N2: Part1.D2, LED1.anode
  N3: Part1.5V, T1.+Vs
  N4: LED1.cathode, R1.Pin_1
